# Fritzing sketch workshop1 (saved by Fritzing 0.9.3b)
circuit board: 8.46667cm x 5.64444cm
breadboards: 1

parts:
  Part1 = Adafruit Pro Trinket 5V 16MHz [part_number="Adafruit #2000"]
  SP1 = SPEAKER [package=pcb_mount_speaker]
  R2 = Resistor [tolerance=±5% resistance=220 package="0805 [SMD]"]
  R1 = PHOTOCELL [package=photocell]

nets:
  N1: Part1.GND, SP1.+, R2.Pin_0
  N2: Part1.+5V, R1.P$2
  N3: Part1.D9, SP1.-
  N4: Part1.A0, R2.Pin_1, R1.P$1

custom parts:
  Adafruit Pro Trinket 5V 16MHz: Trinket's got a big sister in town - the Pro Trinket 5V! Pro Trinket combines everything you love about Trinket with the familiarity of the common core Arduino chip, the ATmega328. It's like an Arduino Pro Mini with more pins and USB tossed in, so delicious. Trinket's a year old now, and while its been great to see tons of tiny projects, sometimes you just need more pins, more FLASH, and more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

// code stored in the sketch: simple_photosensitive_audio.ino
int photosensorPin = 0;
int piezoPin = 9;

int val = 0;

void setup() {
  pinMode(piezoPin, OUTPUT);
}

void loop() {
  digitalWrite(piezoPin, LOW);
  val = analogRead(photosensorPin);
  val = val/2;

  for( int i=0; i<50; ++i){// play it for 50 cycles
    digitalWrite(piezoPin, HIGH);
    delayMicroseconds(val);
    digitalWrite(piezoPin, LOW);
    delayMicroseconds(val);
  }
}
